# Fritzing sketch lightsensorDiagram (saved by Fritzing 0.9.3b)
breadboards: 1

parts:
  R1 = Photocell (LDR) [package=THT]
  R2 = Trimmer Potentiometer [maximum_resistance=10kΩ package=THT]
  Part1 = Arduino Uno (Rev3)
  R3 = Resistor [tolerance=±5% resistance=220 package=THT]
  J1 = Piezo Speaker

nets:
  N1: R1.pin_0, Part1.GND, R3.Pin_0, J1.pin1
  N2: R1.pin_1, R2.wiper
  N3: R2.leg1, Part1.5V
  N4: R2.leg2, Part1.A0, R3.Pin_1
  N5: Part1.D12/MISO, J1.pin2
